// Logisim project 4-bit-ALU-Simulation.circ as structural Verilog: 1 circuit, main circuit main
module main (
  input  [3:0] Number_A,
  input  [3:0] Nmuber_B,
  input  [2:0] opcode,
  output [3:0] Output
);

  wire [3:0] adder_1_out, divider_1_out, multiplier_1_out, subtractor_1_out;

  Adder #(.width(4)) adder_1 (.a(Number_A), .b(Nmuber_B), .out(adder_1_out));  // open: cin, cout
  Subtractor #(.width(4)) subtractor_1 (.a(Number_A), .b(Nmuber_B), .out(subtractor_1_out));  // open: bin, bout
  Multiplier #(.width(4)) multiplier_1 (.a(Number_A), .b(Nmuber_B), .out(multiplier_1_out));  // open: cin, cout
  Divider #(.width(4)) divider_1 (.a(Number_A), .b(Nmuber_B), .out(divider_1_out));  // open: upper, rem
  Multiplexer #(.select(3), .width(4), .enable("false")) multiplexer_1 (
    .in0(adder_1_out), .in1(subtractor_1_out), .in2(multiplier_1_out), .in3(divider_1_out), .out(Output),
    .sel(opcode));  // open: in4, in5, in6, in7
endmodule
