// Logisim project 8-bit adder-subtractor CLA.circ as structural Verilog: 1 circuit, main circuit main
module main (
  input  A3,
  input  A2,
  input  A1,
  input  A0,
  input  B3,
  input  B2,
  input  B1,
  input  B0,
  input  C_1,
  input  C3,
  output out_11,
  output out_12,
  output out_13,
  output out_14
);

  wire and_1_out, and_2_out, and_3_out, and_4_out, and_5_out, and_6_out, and_7_out, and_8_out, and_9_out,
       and_10_out, and_11_out, and_12_out, and_13_out, and_14_out, or_1_out, or_2_out, or_3_out, or_4_out,
       xor_1_out, xor_2_out, xor_3_out, xor_4_out;

  xor xor_1 (xor_1_out, A0, B0);
  and and_1 (and_1_out, A0, B0);
  xor xor_2 (xor_2_out, A1, B1);
  and and_2 (and_2_out, A1, B1);
  xor xor_3 (xor_3_out, A2, B2);
  and and_3 (and_3_out, A2, B2);
  xor xor_4 (xor_4_out, A3, B3);
  and and_4 (and_4_out, A3, B3);
  and and_5 (and_5_out, xor_1_out, C_1);
  and and_6 (and_6_out, xor_2_out, xor_1_out, C_1);
  and and_7 (and_7_out, xor_2_out, and_1_out);
  and and_8 (and_8_out, xor_3_out, xor_2_out, xor_1_out, C_1);
  and and_9 (and_9_out, xor_3_out, xor_2_out, and_1_out);
  and and_10 (and_10_out, xor_3_out, and_2_out);
  and and_11 (and_11_out, xor_4_out, xor_3_out, xor_2_out, xor_1_out, C_1);
  and and_12 (and_12_out, xor_4_out, xor_3_out, xor_2_out, and_1_out);
  and and_13 (and_13_out, xor_4_out, xor_3_out, and_2_out);
  and and_14 (and_14_out, xor_4_out, and_3_out);
  or or_1 (or_1_out, and_5_out, and_1_out);
  or or_2 (or_2_out, and_6_out, and_7_out, and_2_out);
  or or_3 (or_3_out, and_8_out, and_9_out, and_10_out, and_3_out);
  or or_4 (or_4_out, and_11_out, and_12_out, and_13_out, and_14_out, and_4_out);
  xor xor_5 (out_14, C_1, xor_1_out);
  xor xor_6 (out_13, or_1_out, xor_2_out);
  xor xor_7 (out_12, or_2_out, xor_3_out);
  xor xor_8 (out_11, or_3_out, xor_4_out);

  // Notes on the sheet:
  //   P0
  //   G0
  //   P1
  //   G1
  //   P2
  //   G2
  //   P3
  //   G3
  //   P0.C-1
  //   P1.P0.C-1
  //   P1G0
  //   P2.P1.P0.C-1
  //   P2.P1.G0
  //   P2.G1
  //   P3.P2.P1.P0.C-1
  //   P3.P2.P1.G0
  //   P3.P2.G1
  //   P3.G2
  //   C0
  //   C1
  //   C2
  //   S0
  //   S1
  //   S2
  //   S3
endmodule
